# Fritzing sketch wiring (saved by Fritzing 0.9.0b)
circuit board: 8.46667cm x 5.64444cm
breadboards: 1

parts:
  Raspberry_Pi1 = Raspberry Pi B rev2
  S1 = Pushbutton [package="[SMD]"]
  S2 = Pushbutton [package="[SMD]"]
  R1 = Resistor [tolerance=±5% resistance=220 package=THT]
  R2 = Resistor [tolerance=±5% resistance=220 package=THT]

nets:
  N1: Raspberry_Pi1.3V3, S1.Pin_3, S1.Pin_4, S2.Pin_3, S2.Pin_4
  N2: Raspberry_Pi1.GND, R1.Pin_0, R2.Pin_0
  N3: Raspberry_Pi1.GPIO_24, S1.Pin_2, R2.Pin_1
  N4: Raspberry_Pi1.GPIO_8, S2.Pin_1, S2.Pin_2, R1.Pin_1

notes:
  Red Robot
  Blue Robot
